# Fritzing sketch sprinkler controller (saved by Fritzing 0.9.4)

parts:
  U1 = LCD-16X2 [package=lcd-16x2]  # not connected
  Part2 = Adafruit PCF8523 RTC [part_number="Adafruit #3295"]
  U2 = atmega328 [package=dip]
  S1 = Pushbutton [package="[THT]"]
  S2 = Pushbutton [package="[THT]"]
  switch1 = RM-series Subminiature Rotary Switch
  R1 = Resistor [tolerance=±5% resistance=2.2k package=THT]
  R2 = Resistor [tolerance=±5% resistance=220 package=THT]
  R3 = Resistor [tolerance=±5% resistance=470 package=THT]
  R4 = Resistor [tolerance=±5% resistance=680 package=THT]
  R5 = Resistor [tolerance=±5% resistance=1k package=THT]
  R7 = Resistor [tolerance=±5% resistance=3.3k package=THT]
  R8 = Resistor [tolerance=±5% resistance=220 package=THT]
  R9 = Resistor [tolerance=±5% resistance=220 package=THT]
  Part3 = Arduino Nano (Rev3.0)
  R6 = Resistor [tolerance=±5% resistance=2.2k package=THT]

nets:
  N1: Part2.SCL, Part3.A5
  N2: Part2.SDA, Part3.A4
  GND: Part2.GND, Part3.GND
  N3: U2.D0_(RX), Part3.D10
  N4: U2.VCC, R1.Pin_1
  N5: S1.Pin_1, S1.Pin_2, R8.Pin_0, Part3.D3
  N6: S2.Pin_1, S2.Pin_2, R9.Pin_0, Part3.D2
  N7: switch1.1, R1.Pin_0, R2.Pin_1, Part3.A0
  N8: switch1.2, R2.Pin_0, R3.Pin_0
  N9: switch1.3, R3.Pin_1, R4.Pin_1
  N10: switch1.4, R4.Pin_0, R5.Pin_0
  N11: switch1.5, R5.Pin_1, R6.Pin_1
  N12: switch1.6, R7.Pin_0, R6.Pin_0
  N13: switch1.7, R7.Pin_1
  N14: R8.Pin_1, R9.Pin_1

custom parts:
  Adafruit PCF8523 RTC: This is a great battery-backed real time clock (RTC) that allows your microcontroller project to keep track of time even if it is reprogrammed, or if the power is lost. Perfect for datalogging, clock-building, time stamping, timers and alarms, etc. Equipped with PCF8523 RTC - it can run from 3.3V or 5V power & logic! Works great with an Arduino using our RTC library, with CircuitPython or with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
